# Fritzing sketch Driver LED BJT Temp (saved by Fritzing 0.9.2b)
circuit board: 8.53488cm x 5.63626cm
breadboards: 1

parts:
  Power_plug1 = Power plug
  Q1 = TRANSISTOR_NPN [part_number=bc547 package=to-92-ammo]
  Q2 = TRANSISTOR_NPN [part_number=bc547 package=to-92-ammo]
  Q3 = TRANSISTOR_NPN [part_number=bc547 package=to-92-ammo]
  Q4 = TRANSISTOR_NPN [part_number=bc547 package=to-92-ammo]
  T1 = LM35 Temperature Sensor [package="TO92 [THT]"]
  T2 = LM35 Temperature Sensor [package="TO92 [THT]"]
  T3 = LM35 Temperature Sensor [package="TO92 [THT]"]
  R1 = Resistor [tolerance=±5% resistance=1k package=THT]
  R2 = Resistor [tolerance=±5% resistance=1k package=THT]
  R3 = Resistor [tolerance=±5% resistance=1k package=THT]
  R4 = Resistor [tolerance=±5% resistance=1k package=THT]
  LED1 = LEDs [package=led10mm]
  LED2 = LEDs [package=led10mm]
  LED3 = LEDs [package=led10mm]
  LED4 = LEDs [package=led10mm]
  T4 = LM35 Temperature Sensor [package="TO92 [THT]"]
  Raspberry_Pi1 = Raspberry Pi 2
  A1 = Header 1 [package=1x01_offset]
  A2 = Header 1 [package=1x01_offset]
  A3 = Header 1 [package=1x01_offset]
  A4 = Header 1 [package=1x01_offset]
  GND = Header 1 [package=1x01_offset]

nets:
  GND: Power_plug1.GND, Q1.E, Q2.E, Q3.E, Q4.E, T1.GND, T2.GND, T3.GND, T4.GND, Raspberry_Pi1.GND, GND.1
  N1: Power_plug1.VCC, T1.+Vs, T2.+Vs, T3.+Vs, LED1.C, LED2.C, LED3.C, LED4.C, T4.+Vs
  N2: Q1.B, R1.Pin_0
  N3: Q1.C, LED1.A
  N4: Q2.B, R2.Pin_0
  N5: Q2.C, LED2.A
  N6: Q3.B, R3.Pin_0
  N7: Q3.C, LED3.A
  N8: Q4.B, R4.Pin_0
  N9: Q4.C, LED4.A
  N10: T1.Vout, A1.1
  N11: T2.Vout, A2.1
  N12: T3.Vout, A3.1
  N13: R1.Pin_1, Raspberry_Pi1.GPIO5
  N14: R2.Pin_1, Raspberry_Pi1.GPIO6
  N15: R3.Pin_1, Raspberry_Pi1.GPIO13
  N16: R4.Pin_1, Raspberry_Pi1.GPIO19
  N17: T4.Vout, A4.1

// code stored in the sketch: Media_LM35_4CH.ino
int n_campioni;

float valore1;
float media1;
int temp1;

float valore2;
float media2;
int temp2;

float valore3;
float media3;
int temp3;

float valore4;
float media4;
int temp4;

void setup()
{
  analogReference(INTERNAL);
}

void loop(){

n_campioni++;

valore1 = analogRead(A1);
valore2 = analogRead(A2);
valore3 = analogRead(A3);
valore4 = analogRead(A4);

media1 = media1 + (valore1 - media1) / n_campioni;
media2 = media2 + (valore2 - media2) / n_campioni;
media3 = media3 + (valore3 - media3) / n_campioni;
media4 = media4 + (valore4 - media4) / n_campioni;

if (n_campioni>=512){
  temp1=(1.1 * media1 * 100.0) / 1024.0;
  temp2=(1.1 * media2 * 100.0) / 1024.0;
  temp3=(1.1 * media3 * 100.0) / 1024.0;
  temp4=(1.1 * media4 * 100.0) / 1024.0;
  Serial.begin(9600);
  Serial.print(temp1,DEC);
  Serial.print(" ");
  Serial.print(temp2,DEC);
  Serial.print(" ");
  Serial.print(temp3,DEC);
  Serial.print(" ");
  Serial.print(temp4,DEC);
  Serial.print("\n");
  Serial.end();
  n_campioni=0;
}
}
