# Fritzing sketch Driver LED Ponte H (saved by Fritzing 0.9.2b)
breadboards: 1

parts:
  IC1 = H-Bridge [package=THT]
  Power_plug1 = Power plug
  Raspberry_Pi1 = Raspberry Pi 2
  LED1 = smd LED [color="Red (633nm)" package="1206 [SMD]"]
  LED2 = smd LED [color="Red (633nm)" package="1206 [SMD]"]
  LED3 = smd LED [color="Red (633nm)" package="1206 [SMD]"]
  LED4 = smd LED [color="Red (633nm)" package="1206 [SMD]"]

nets:
  N1: IC1.1_2EN, IC1.3_4EN, IC1.VCC1, Raspberry_Pi1.5V
  N2: IC1.1A, Raspberry_Pi1.GPIO13
  N3: IC1.1Y, LED3.anode
  GND: IC1.GND1, IC1.GND2, IC1.GND3, IC1.GND4, Power_plug1.GND, Raspberry_Pi1.GND, LED1.cathode, LED2.cathode, LED3.cathode, LED4.cathode
  N4: IC1.2Y, LED4.anode
  N5: IC1.2A, Raspberry_Pi1.GPIO19
  N6: IC1.VCC2, Power_plug1.VCC
  N7: IC1.3A, Raspberry_Pi1.GPIO5
  N8: IC1.3Y, LED1.anode
  N9: IC1.4Y, LED2.anode
  N10: IC1.4A, Raspberry_Pi1.GPIO6
