# Fritzing sketch Dual LM7805 Pi ExpoScuola (saved by Fritzing 0.9.2b)
circuit board: 1.64337cm x 2.11668cm

parts:
  U1 = Voltage Regulator - 5V [part_number=LM7805 package="TO220 [THT]"]
  C1 = Ceramic Capacitor [capacitance=100nF package="100 mil [THT, multilayer]"]
  D2 = Diode [part_number=1N5061 package=diode-1n4148]
  C2 = Ceramic Capacitor [capacitance=100nF package="100 mil [THT, multilayer]"]
  VCC3 = Battery block 9V
  U2 = Voltage Regulator - 5V [part_number=LM7805 package="TO220 [THT]"]
  VCC1 = Battery block 9V
  VCC2 = Battery block 9V
  JP3 = Header 3 [package=screwterminal-3.5mm-3_lock.007s]
  D1 = Diode [part_number=1N5061 package=diode-1n4148]

nets:
  N1: U1.input_voltage, C1.1, VCC3.+, U2.input_voltage, VCC1.+, VCC2.+, JP3.1
  GND: U1.GND, C1.0, C2.0, VCC3.-, U2.GND, VCC1.-, VCC2.-, JP3.2
  N2: U1.output_voltage, D1.A
  N3: D2.A, U2.output_voltage
  N4: D2.C, C2.1, JP3.3, D1.C
